// Logisim project cpu.circ as structural Verilog: 9 circuits, main circuit main
module main (
  input  [7:0] in_1
);

  wire and_1_out, and_2_out, and_3_out, and_4_out, and_5_out, button_1_out, clock_1_out, not_1_out,
       not_2_out, not_3_out, not_4_out, not_5_out, not_6_out, not_7_out, not_8_out, not_9_out, not_10_out,
       not_11_out, not_12_out, not_13_out, not_14_out, not_15_out, or_1_out, or_2_out, Reset_all_out,
       Reset_PC_out, transistor_1_out, transistor_2_out;
  wire [4:0] IR_data;
  wire [7:0] alu_1_out_18, Data__RAM_data, demultiplexer_1_out1, demultiplexer_2_out1, multiplexer_1_out,
       multiplexer_2_out, PC_Adder_out_3, PC_q, Register_A_q, Register_B_2_q, Register_B_q;
  wire [7:5] IR_data_2;

  and and_1 (and_1_out, IR_data[0], IR_data[3], not_3_out, not_2_out, not_1_out);
  not not_1 (not_1_out, IR_data[4]);
  not not_2 (not_2_out, IR_data[2]);
  not not_3 (not_3_out, IR_data[1]);
  Multiplexer_part #(.width(8), .enable("false")) multiplexer_1 (
    .in0(in_1), .in1(Data__RAM_data), .out(multiplexer_1_out), .sel(and_1_out));
  RAM #(.bus("separate"), .Select("low")) Data__RAM (
    .addr(PC_q), .din(Register_B_2_q), .data(Data__RAM_data), .str(and_2_out), .clk(clock_1_out),
    .clr(Reset_all_out));  // open: sel, ld
  not not_4 (not_4_out, IR_data[4]);
  and and_2 (and_2_out, not_4_out, not_5_out, not_8_out, IR_data[3], IR_data[1]);
  and and_3 (and_3_out, not_6_out, not_7_out, IR_data[2], IR_data[1], not_9_out);
  not not_5 (not_5_out, IR_data[2]);
  not not_6 (not_6_out, IR_data[3]);
  not not_7 (not_7_out, IR_data[4]);
  not not_8 (not_8_out, IR_data[0]);
  TTY tty_1 (.data(multiplexer_1_out[6:0]), .clk(clock_1_out), .clr(or_1_out));  // open: we
  or or_1 (or_1_out, Reset_all_out, button_1_out);
  Button button_1 (.out(button_1_out));
  Demultiplexer #(.width(8), .enable("false")) demultiplexer_1 (
    .out1(demultiplexer_1_out1), .in(Data__RAM_data), .sel(transistor_1_out));  // open: out0
  and and_4 (and_4_out, not_11_out, not_10_out, IR_data[2], IR_data[1], IR_data[0]);
  not not_9 (not_9_out, IR_data[0]);
  not not_10 (not_10_out, IR_data[3]);
  not not_11 (not_11_out, IR_data[4]);
  Demultiplexer #(.width(8), .enable("false")) demultiplexer_2 (
    .out1(demultiplexer_2_out1), .in(Data__RAM_data), .sel(transistor_2_out));  // open: out0
  Transistor #(.\type ("n")) transistor_1 (.in(1'b1), .out(transistor_1_out), .gate(and_4_out));
  Transistor #(.\type ("n")) transistor_2 (.in(1'b1), .out(transistor_2_out), .gate(and_5_out));
  and and_5 (and_5_out, IR_data[3], not_12_out, not_14_out, not_13_out, not_15_out);
  not not_12 (not_12_out, IR_data[4]);
  not not_13 (not_13_out, IR_data[1]);
  not not_14 (not_14_out, IR_data[2]);
  not not_15 (not_15_out, IR_data[0]);
  Clock clock_1 (.out(clock_1_out));
  Button Reset_all (.out(Reset_all_out));
  Button Reset_PC (.out(Reset_PC_out));
  Multiplexer_part #(.width(8), .enable("false")) multiplexer_2 (
    .in0(PC_Adder_out_3), .in1(Data__RAM_data), .out(multiplexer_2_out), .sel(and_3_out));
  Register #(.Select("low")) PC (.D(multiplexer_2_out), .Q(PC_q), .clk(clock_1_out), .clr(or_2_out));  // open: en
  or or_2 (or_2_out, Reset_PC_out, Reset_all_out);
  Register #(.Select("low")) Register_A (
    .D(demultiplexer_2_out1), .Q(Register_A_q), .clk(clock_1_out), .clr(Reset_all_out));  // open: en
  Register #(.Select("low")) Register_B (
    .D(demultiplexer_1_out1), .Q(Register_B_q), .clk(clock_1_out), .clr(Reset_all_out));  // open: en
  ROM #(.Select("low")) IR (.addr(PC_q), .data({IR_data_2, IR_data}));
  PC PC_Adder (.in_1(PC_q), .Reset(Reset_all_out), .out_3(PC_Adder_out_3));
  ALU alu_1 (
    .in_9(Register_B_q[7]), .Daten_2(Register_B_q[6]), .in_11(Register_B_q[5]), .in_12(Register_B_q[4]),
    .in_13(Register_B_q[3]), .in_14(Register_B_q[2]), .in_15(Register_B_q[1]), .Low_2(Register_B_q[0]),
    .out_18(alu_1_out_18), .in_17(IR_data), .in_1(Register_A_q[7]), .Daten(Register_A_q[6]),
    .in_3(Register_A_q[5]), .in_4(Register_A_q[4]), .in_5(Register_A_q[3]), .in_6(Register_A_q[2]),
    .in_7(Register_A_q[1]), .Low(Register_A_q[0]));
  Register #(.Select("low")) Register_B_2 (
    .D(alu_1_out_18), .Q(Register_B_2_q), .clk(clock_1_out), .clr(Reset_all_out));  // open: en

  // Notes on the sheet:
  //   contents of IR (hex, n*v repeats v):
  //   0 7 8 1 0 6*9 6
endmodule

module Halbaddierer (
  input  A,
  input  B,
  output Ergebnis,
  output Carry
);

  xor xor_1 (Ergebnis, A, B);
  and and_1 (Carry, A, B);
endmodule

module VollAddierer (
  input  A,
  input  B,
  input  C,
  output Ergebnis,
  output Carry
);

  wire and_1_out, and_2_out, xor_1_out;

  xor xor_1 (xor_1_out, A, B);
  and and_1 (and_1_out, A, B);
  xor xor_2 (Ergebnis, xor_1_out, C);
  and and_2 (and_2_out, C, xor_1_out);
  or or_1 (Carry, and_2_out, and_1_out);
endmodule

module _16_Bit_Addierer (
  input  in_1,
  input  in_2,
  input  in_3,
  input  in_4,
  input  in_5,
  input  in_6,
  input  in_7,
  input  in_8,
  input  in_9,
  input  in_10,
  input  in_11,
  input  in_12,
  input  in_13,
  input  in_14,
  input  in_15,
  input  in_16,
  output out_17,
  output out_18,
  output out_19,
  output out_20,
  output out_21,
  output out_22,
  output out_23,
  output out_24
);

  wire halbaddierer_1_carry, volladdierer_1_carry, volladdierer_2_carry, volladdierer_3_carry,
       volladdierer_4_carry, volladdierer_5_carry, volladdierer_6_carry, volladdierer_7_carry;

  Halbaddierer halbaddierer_1 (.A(in_8), .B(in_16), .Ergebnis(out_24), .Carry(halbaddierer_1_carry));
  VollAddierer volladdierer_1 (
    .A(in_7), .B(in_15), .C(halbaddierer_1_carry), .Ergebnis(out_23), .Carry(volladdierer_1_carry));
  VollAddierer volladdierer_2 (
    .A(in_14), .B(in_6), .C(volladdierer_1_carry), .Ergebnis(out_22), .Carry(volladdierer_2_carry));
  VollAddierer volladdierer_3 (
    .A(in_5), .B(in_13), .C(volladdierer_2_carry), .Ergebnis(out_21), .Carry(volladdierer_3_carry));
  VollAddierer volladdierer_4 (
    .A(in_12), .B(in_4), .C(volladdierer_3_carry), .Ergebnis(out_20), .Carry(volladdierer_4_carry));
  VollAddierer volladdierer_5 (
    .A(in_11), .B(in_3), .C(volladdierer_4_carry), .Ergebnis(out_19), .Carry(volladdierer_5_carry));
  VollAddierer volladdierer_6 (
    .A(in_10), .B(in_2), .C(volladdierer_5_carry), .Ergebnis(out_18), .Carry(volladdierer_6_carry));
  VollAddierer volladdierer_7 (
    .A(in_9), .B(in_1), .C(volladdierer_6_carry), .Ergebnis(out_17), .Carry(volladdierer_7_carry));
endmodule

module ALU (
  input  in_1,
  input  Daten,
  input  in_3,
  input  in_4,
  input  in_5,
  input  in_6,
  input  in_7,
  input  Low,
  input  in_9,
  input  Daten_2,
  input  in_11,
  input  in_12,
  input  in_13,
  input  in_14,
  input  in_15,
  input  Low_2,
  input  [4:0] in_17,
  output [7:0] out_18
);

  wire [7:0] Adder_out_24, divider_1_out, multiplier_1_out, subtractor_1_out;

  _16_Bit_Addierer Adder (
    .in_1(in_9), .in_2(Daten_2), .in_3(in_11), .in_4(in_12), .in_5(in_13), .in_6(in_14), .in_7(in_15),
    .in_8(Low_2), .in_9(in_1), .in_10(Daten), .in_11(in_3), .in_12(in_4), .in_13(in_5), .in_14(in_6),
    .in_15(in_7), .in_16(Low), .out_17(Adder_out_24[7]), .out_18(Adder_out_24[6]), .out_19(Adder_out_24[5]),
    .out_20(Adder_out_24[4]), .out_21(Adder_out_24[3]), .out_22(Adder_out_24[2]), .out_23(Adder_out_24[1]),
    .out_24(Adder_out_24[0]));
  Subtractor subtractor_1 (
    .a({in_1, Daten, in_3, in_4, in_5, in_6, in_7, Low}),
    .b({in_9, Daten_2, in_11, in_12, in_13, in_14, in_15, Low_2}), .out(subtractor_1_out));  // open: bin, bout
  Multiplier multiplier_1 (
    .a({in_9, Daten_2, in_11, in_12, in_13, in_14, in_15, Low_2}),
    .b({in_1, Daten, in_3, in_4, in_5, in_6, in_7, Low}), .out(multiplier_1_out));  // open: cin, cout
  Divider divider_1 (
    .a({in_1, Daten, in_3, in_4, in_5, in_6, in_7, Low}),
    .b({in_9, Daten_2, in_11, in_12, in_13, in_14, in_15, Low_2}), .out(divider_1_out));  // open: upper, rem
  Multiplexer_part #(.select(5), .width(8), .enable("false")) multiplexer_1 (
    .in1(Adder_out_24), .in2(subtractor_1_out), .in3(multiplier_1_out), .in4(divider_1_out), .out(out_18),
    .sel(in_17));  // open: in0, in5, in6, in7, in8, in9, in10, in11, in12, in13, in14, in15, in16, in17, in18, in19, in20, in21, in22, in23, in24, in25, in26, in27, in28, in29, in30, in31

  // Notes on the sheet:
  //   Sub
  //   Multi
  //   Devide
endmodule

module Multiplexer (
  input  in_1,
  input  Eingang_2,
  input  in_3,
  output out_4
);

  wire and_1_out, and_2_out, not_1_out;

  and and_1 (and_1_out, in_1, not_1_out);
  not not_1 (not_1_out, in_3);
  and and_2 (and_2_out, Eingang_2, in_3);
  or or_1 (out_4, and_1_out, and_2_out);

  // Notes on the sheet:
  //   Eingang 1
  //   OP-Code
endmodule

module _8_Bit_Multiplexer (
  input  [7:0] in_1,
  input  [7:0] in_2,
  input  [7:0] in_3,
  input  [7:0] in_4,
  output [7:0] out_5
);

  wire and_1_out, and_2_out, not_1_out, not_2_out, not_3_out, not_4_out, not_5_out, not_6_out, not_7_out,
       not_8_out, not_9_out, not_10_out, not_11_out, not_12_out, not_13_out, not_14_out;
  wire [7:0] multiplexer_1_out, multiplexer_2_out;

  not not_1 (not_1_out, in_1[1]);
  not not_2 (not_2_out, in_1[2]);
  not not_3 (not_3_out, in_1[3]);
  not not_4 (not_4_out, in_1[4]);
  not not_5 (not_5_out, in_1[5]);
  not not_6 (not_6_out, in_1[6]);
  not not_7 (not_7_out, in_1[7]);
  not not_8 (not_8_out, in_1[0]);
  not not_9 (not_9_out, in_1[2]);
  not not_10 (not_10_out, in_1[3]);
  not not_11 (not_11_out, in_1[4]);
  not not_12 (not_12_out, in_1[5]);
  not not_13 (not_13_out, in_1[6]);
  not not_14 (not_14_out, in_1[7]);
  and and_1 (and_1_out, in_1[0], not_1_out, not_2_out, not_3_out, not_4_out, not_5_out, not_6_out, not_7_out);
  and and_2 (and_2_out, not_8_out, in_1[1], not_9_out, not_10_out, not_11_out, not_12_out, not_13_out, not_14_out);
  Multiplexer_part #(.width(8), .enable("false")) multiplexer_1 (
    .in0(in_2), .in1(in_3), .out(multiplexer_1_out), .sel(and_1_out));
  Multiplexer_part #(.width(8), .enable("false")) multiplexer_2 (
    .in0(multiplexer_1_out), .in1(in_4), .out(multiplexer_2_out), .sel(and_2_out));
  assign out_5 = multiplexer_1_out | multiplexer_2_out;  // OR_Gate or_1, 8 bits wide

  // Notes on the sheet:
  //   OP-Code
  //   Data 1
  //   Data 2
  //   Data 3
endmodule

module PC (
  input  [7:0] in_1,
  input  Reset,
  output [7:0] out_3
);

  wire [0:0] not_1_out;

  not not_1 (not_1_out[0], Reset);
  Adder adder_1 (.a({{7{1'b0}}, not_1_out[0]}), .b(in_1), .out(out_3));  // open: cin, cout
endmodule

module Instruction_Fetch (
  input  [4:0] in_1
);

  wire not_1_out, not_2_out, not_3_out, not_4_out, not_5_out, not_6_out, not_7_out, not_8_out, not_9_out,
       not_10_out, not_11_out, not_12_out, not_13_out, not_14_out, not_15_out, undriven, undriven_2,
       undriven_3, undriven_4, undriven_5, undriven_6, undriven_7, undriven_8;

  // AND_Gate and_1 has open pins: in2=not_3_out, in3=not_2_out, in4=not_1_out, out=open
  // NOT_Gate not_1 has open pins: in=open, out=not_1_out
  // NOT_Gate not_2 has open pins: in=open, out=not_2_out
  // NOT_Gate not_3 has open pins: in=open, out=not_3_out
  // AND_Gate and_2 has open pins: in0=not_4_out, in1=not_5_out, in2=not_6_out, in3=undriven_2, in4=undriven_3, out=open
  not not_4 (not_4_out, undriven);
  not not_5 (not_5_out, undriven_4);
  // NOT_Gate not_6 has open pins: in=open, out=not_6_out
  // AND_Gate and_3 has open pins: in0=not_8_out, in1=not_9_out, in2=undriven_4, in3=undriven_3, in4=not_7_out, out=open
  // NOT_Gate not_7 has open pins: in=open, out=not_7_out
  not not_8 (not_8_out, undriven_2);
  not not_9 (not_9_out, undriven);
  // AND_Gate and_4 has open pins: in0=not_10_out, in1=not_11_out, in2=undriven_4, in3=undriven_5, out=open
  not not_10 (not_10_out, undriven);
  not not_11 (not_11_out, undriven_2);
  // NOT_Gate not_12 has open pins: in=open, out=not_12_out
  // AND_Gate and_5 has open pins: in0=undriven_6, in1=not_12_out, in2=not_13_out, in3=not_14_out, in4=not_15_out, out=open
  not not_13 (not_13_out, undriven_7);
  not not_14 (not_14_out, undriven_8);
  // NOT_Gate not_15 has open pins: in=open, out=not_15_out
endmodule
